// Logisim project theremin_toplevel.circ as structural Verilog: 1 circuit, main circuit theremin_toplevel
module theremin_toplevel (
  input  clk,
  input  PMOD_0_1,
  input  PMOD_1_1,
  input  [7:0] switches,
  input  [3:0] buttons,
  output PMOD_0_0,
  output PMOD_0_2,
  output PMOD_1_0,
  output PMOD_1_2,
  output [6:0] cathodes,
  output anode0,
  output anode1,
  output anode2,
  output anode3,
  output PMOD_2_0,
  output PMOD_2_1,
  output PMOD_2_2,
  output PMOD_2_3
);

  wire not_1_out, not_2_out, tlc548_1_cs, tlc548_1_io_clock, tlc548_2_cs, tlc548_2_io_clock;
  wire [7:0] bit_extender_1_out, CPU_Interface_1_periphread6, CPU_Interface_1_periphread7,
       dist_correct_1_data, dist_correct_2_data, tlc548_1_value, tlc548_2_value;
  wire [15:0] adder_1_out, bit_extender_2_out, shifter_1_out, sound_gen_1_sound;

  not not_1 (not_1_out, PMOD_0_1);
  not not_2 (not_2_out, PMOD_1_1);
  not not_3 (PMOD_0_0, tlc548_1_cs);
  tlc548 tlc548_1 (
    .clk(clk), .data_in(not_1_out), .cs(tlc548_1_cs), .io_clock(tlc548_1_io_clock), .value(tlc548_1_value));
  not not_4 (PMOD_0_2, tlc548_1_io_clock);
  not not_5 (PMOD_1_0, tlc548_2_cs);
  tlc548 tlc548_2 (
    .clk(clk), .data_in(not_2_out), .cs(tlc548_2_cs), .io_clock(tlc548_2_io_clock), .value(tlc548_2_value));
  not not_6 (PMOD_1_2, tlc548_2_io_clock);
  assign bit_extender_1_out = {{4{buttons[3]}}, buttons};  // Bit_Extender bit_extender_1
  dist_correct dist_correct_1 (.addr(tlc548_1_value), .data(dist_correct_1_data));
  dist_correct dist_correct_2 (.addr(tlc548_2_value), .data(dist_correct_2_data));
  CPU_Interface CPU_Interface_1 (
    .clk(clk), .PeriphWrite0(dist_correct_1_data), .PeriphWE0(1'b1), .PeriphWrite1(dist_correct_2_data),
    .PeriphWE1(1'b1), .PeriphRead6(CPU_Interface_1_periphread6), .PeriphRead7(CPU_Interface_1_periphread7));  // open: Reset, PeriphWrite2, PeriphWE2, PeriphWrite3, PeriphWE3, PeriphWrite4, PeriphWE4, PeriphWrite5, PeriphWE5, PeriphWrite6, PeriphWE6, PeriphWrite7, PeriphWE7, PeriphRead0, PeriphRead1, PeriphRead2, PeriphRead3, PeriphRead4, PeriphRead5
  assign bit_extender_2_out = {{8{CPU_Interface_1_periphread6[7]}}, CPU_Interface_1_periphread6};  // Bit_Extender bit_extender_2
  Shifter #(.width(16)) shifter_1 (.in(bit_extender_2_out), .\dist (4'b0010), .out(shifter_1_out));
  Adder #(.width(16)) adder_1 (.a(16'h85), .b(shifter_1_out), .out(adder_1_out));  // open: cin, cout
  sound_gen sound_gen_1 (
    .clk(clk), .phase_add(adder_1_out), .waveform(bit_extender_1_out),
    .amplitude_in({1'b0, CPU_Interface_1_periphread7, {7{1'b0}}}), .sound(sound_gen_1_sound));
  bytes_display bytes_debug (
    .octet1(sound_gen_1_sound[15:8]), .octet1_enable(1'b1), .octet2(sound_gen_1_sound[7:0]),
    .octet2_enable(1'b1), .reset(1'b0), .clk(clk), .cathodes(cathodes), .anode0(anode0), .anode1(anode1),
    .anode2(anode2), .anode3(anode3));
  cs4344_mono cs4344_mono_1 (
    .clk(clk), .rst(1'b0), .audio_in(sound_gen_1_sound), .SDOUT(PMOD_2_3), .SCLK(PMOD_2_2), .MCLK(PMOD_2_0),
    .LRCK(PMOD_2_1));  // open: done
endmodule
